# Fritzing sketch Project Anukul_ciruit_diagram (saved by Fritzing 0.9.3b)
breadboards: 1

parts:
  Part1 = Arduino Uno (Rev3)
  Grove1 = Grove Light Sensor
  Part4 = Soil Moisture Sensor
  Part5 = MicroSD Card Module
  DS1 = DS18B20 1-Wire Temperature Sensor [part_number=DS18B20]
  U3 = LCD-16X2 [package=lcd-16x2_noholes]
  R1 = Resistor [tolerance=±5% resistance=4.7k package="0402 [SMD]"]
  VCC1 = Battery block 9V
  ZS-042_RTC1 = ZS-042 RTC Module

nets:
  N1: Part1.A0, Part4.SIG
  N2: Part1.A4/SDA, ZS-042_RTC1.SDA
  N3: Part1.A5/SCL, ZS-042_RTC1.SCL
  GND: Part1.D8, Part1.D9_PWM, Part1.GND, Grove1.GND, Part4.GND, Part5.GND, DS1.GND, U3.VSS, U3.VO, U3.RS, U3.R_W, U3.E, VCC1.-, ZS-042_RTC1.GND
  N4: Part1.D10_PWM/SS, U3.DB7
  N5: Part1.D11_PWM/MOSI, Part5.MOSI
  N6: Part1.D12/MISO, Part5.MISO
  N7: Part1.D13/SCK, Part5.SCK
  VCC: Part1.D2, Part1.5V, Grove1.VCC, Part4.VCC, Part5.VCC, DS1.DQ, DS1.VDD, R1.Pin_0, R1.Pin_1, ZS-042_RTC1.VCC
  N8: Part1.D3_PWM, Grove1.SIG
  N9: Part1.D4, Part5.CS
  N10: Part1.D5_PWM, U3.DB6
  N11: Part1.D6_PWM, U3.DB5
  N12: Part1.D7, U3.DB3, U3.DB4
  3V3: Part1.3V3, U3.VDD
  N13: Part1.VIN, VCC1.+
